# Fritzing sketch Notification Device (saved by Fritzing 1.0.1rc)

parts:
  M5StackC = M5Stick-C
  U1 = Vibration Motor- ROB-08449 [package=vibe-motor-10mm]
  BATT1 = FKIT-COIN_CELL [package=fkit-lir2450-h]
  M5_Atom_Lite = M5Stick-C
  Part1 = PowerBoost 500 Charger
  VCC1 = Battery

nets:
  N1: M5StackC.5v#6, BATT1.POS
  N2: M5StackC.Gnd, BATT1.NEG
  N3: M5StackC.G33, U1.+
  N4: M5StackC.5v#10, U1.-
  N5: M5_Atom_Lite.5v, Part1.5.0V
  GND: M5_Atom_Lite.Gnd, Part1.GND
  N6: Part1.GND_BAT_IN, VCC1.-
  N7: Part1.VBAT_IN, VCC1.+

notes:
  BLE Scanner for Alert Notification
  BLE Beacon

custom parts:
  M5Stick-C: M5Stick-C is a mini M5Stack, powered by ESP32 pico chip. It is a portable, easy-to-use, open source, IoT development board.
  Battery: Your standard 2x 18650 battery pack (7,4 Volts)
